# Fritzing sketch wiring (saved by Fritzing 0.9.5d)
breadboards: 1

parts:
  VCC1 = Battery block 9V
  R1 = Resistor [tolerance=±5% resistance=10k package="0805 [SMD]"]
  Arduino = Arduino Micro (Rev3)
  IRFZ44N = Basic FET N-Channel [package="DPak [SMD]"]
  R2 = Resistor [tolerance=±5% resistance=10k package="0805 [SMD]"]
  LED1_-_12V = smd LED [color="Red (633nm)" package="1206 [SMD]"]
  S1 = Pushbutton [package="[SMD]"]

nets:
  N1: VCC1.-, R1.Pin_0, IRFZ44N.source
  N2: VCC1.+, LED1_-_12V.anode
  GND: R1.Pin_1, Arduino.GND, IRFZ44N.Gate, R2.Pin_1, S1.Pin_3, S1.Pin_4
  N3: Arduino.D2/SDA, S1.Pin_1, S1.Pin_2
  5V: Arduino.5V, R2.Pin_0
  N4: IRFZ44N.drain, LED1_-_12V.cathode
