# Fritzing sketch fritzing (saved by Fritzing 1.0.2b)
circuit board: 4.3cm x 3.8cm
breadboards: 1

parts:
  Xiao = seeeduino-xiao
  S1 = Pushbutton [package="[THT]"]
  Q1 = NPN-Transistor [package="TO92 [THT]"]
  LED = LED - 3mm [color="Red (633nm)" current=0.030A package="3 mm [THT]"]

nets:
  N1: Xiao.D2, Q1.C
  N2: Xiao.D10, S1.Pin_3, S1.Pin_4
  3.3V: Xiao.3V3, LED.anode
  GND: Xiao.GND, S1.Pin_1, S1.Pin_2, Q1.E
  N3: Q1.B, LED.cathode

notes:
  Big Red Button rev2

custom parts:
  seeeduino-xiao: Seeeduino XIAO processor board.
